// Logisim project CPU8.circ as structural Verilog: 15 circuits, main circuit BOARD
module BOARD (
  input  RESET,
  input  CLOCK
);

  wire and_1_out, and_2_out, and_3_out, and_4_out, and_5_out, and_6_out, and_7_out, and_8_out, clock_1_out,
       controlled_buffer_1_out, dec4_1__0_2, dec4_1__1_2, dec4_1__2_2, dec4_1__3_2, dec4_1__4, dec4_1__5,
       dec4_1__6, dec4_1__7, dec4_1__8, dec4_1__9, dec4_1_a, dec4_1_b, dec4_1_c, dec4_1_d, dec4_1_e_2,
       dec4_1_f, decoder_1_out0, decoder_1_out1, decoder_1_out2, decoder_1_out3, decoder_2_out0,
       decoder_2_out1, decoder_2_out2, decoder_2_out3, decoder_2_out4, decoder_2_out5, decoder_2_out6,
       not_1_out, not_2_out, not_3_out, not_4_out, not_5_out, not_6_out, or_1_out, undriven_2, undriven_6,
       undriven_7, undriven_8, undriven_9, undriven_10, undriven_12;
  wire [1:0] undriven;
  wire [2:0] undriven_3, undriven_4, undriven_5;
  wire [7:0] alu_1_r, controlled_buffer_2_out, controlled_buffer_3_out, controlled_buffer_5_out,
       controlled_buffer_7_out, controlled_buffer_9_out, multiplexer_1_out, multiplexer_2_out, P_q,
       undriven_11, W_q, X_q, Y_q, Z_q;

  Decoder #(.select(2)) decoder_1 (
    .out0(decoder_1_out0), .out1(decoder_1_out1), .out2(decoder_1_out2), .out3(decoder_1_out3),
    .sel(undriven), .en(undriven_2));
  not not_1 (not_1_out, or_1_out);
  Clock clock_1 (.out(clock_1_out));
  LED HALT (.in(or_1_out));
  assign controlled_buffer_1_out = not_1_out ? clock_1_out : 1'bz;  // Controlled_Buffer controlled_buffer_1
  and and_1 (and_1_out, decoder_1_out3, undriven_10);
  assign controlled_buffer_2_out = and_1_out ? Z_q : 8'bz;  // Controlled_Buffer controlled_buffer_2
  not not_2 (not_2_out, and_1_out);
  assign controlled_buffer_3_out = not_2_out ? controlled_buffer_2_out : 8'bz;  // Controlled_Buffer controlled_buffer_3
  // Probe on Z_q
  REG8 Z (.C(and_2_out), ._0(RESET), .D(controlled_buffer_3_out), .Q(Z_q));
  and and_2 (and_2_out, decoder_1_out3, controlled_buffer_1_out);
  and and_3 (and_3_out, decoder_1_out2, undriven_10);
  assign controlled_buffer_2_out = and_3_out ? Y_q : 8'bz;  // Controlled_Buffer controlled_buffer_4
  not not_3 (not_3_out, and_3_out);
  assign controlled_buffer_5_out = not_3_out ? controlled_buffer_2_out : 8'bz;  // Controlled_Buffer controlled_buffer_5
  // Probe on Y_q
  REG8 Y (.C(and_4_out), ._0(RESET), .D(controlled_buffer_5_out), .Q(Y_q));
  and and_4 (and_4_out, decoder_1_out2, controlled_buffer_1_out);
  assign controlled_buffer_2_out = and_6_out ? X_q : 8'bz;  // Controlled_Buffer controlled_buffer_6
  assign controlled_buffer_7_out = not_4_out ? controlled_buffer_2_out : 8'bz;  // Controlled_Buffer controlled_buffer_7
  REG8 X (.C(and_5_out), ._0(RESET), .D(controlled_buffer_7_out), .Q(X_q));
  and and_5 (and_5_out, decoder_1_out1, controlled_buffer_1_out);
  and and_6 (and_6_out, decoder_1_out1, undriven_10);
  not not_4 (not_4_out, and_6_out);
  // Probe on X_q
  and and_7 (and_7_out, decoder_1_out0, undriven_10);
  assign controlled_buffer_2_out = and_7_out ? W_q : 8'bz;  // Controlled_Buffer controlled_buffer_8
  not not_5 (not_5_out, and_7_out);
  assign controlled_buffer_9_out = not_5_out ? controlled_buffer_2_out : 8'bz;  // Controlled_Buffer controlled_buffer_9
  // Probe on W_q
  REG8 W (.C(and_8_out), ._0(RESET), .D(controlled_buffer_9_out), .Q(W_q));
  and and_8 (and_8_out, decoder_1_out0, controlled_buffer_1_out);
  Multiplexer #(.select(3), .width(8)) multiplexer_1 (
    .in0(W_q), .in1(X_q), .in2(Y_q), .in3(Z_q), .in4(controlled_buffer_2_out), .out(multiplexer_1_out),
    .sel(undriven_4), .en(undriven_6));  // open: in5, in6, in7
  Decoder #(.select(3), .enable("false")) decoder_2 (
    .out0(decoder_2_out0), .out1(decoder_2_out1), .out2(decoder_2_out2), .out3(decoder_2_out3),
    .out4(decoder_2_out4), .out5(decoder_2_out5), .out6(decoder_2_out6), .sel(undriven_3));  // open: out7
  Multiplexer #(.select(3), .width(8)) multiplexer_2 (
    .in0(W_q), .in1(X_q), .in2(Y_q), .in3(Z_q), .in4(controlled_buffer_2_out), .out(multiplexer_2_out),
    .sel(undriven_5), .en(undriven_6));  // open: in5, in6, in7
  ALU alu_1 (
    .LSR(decoder_2_out5), .LSL(decoder_2_out6), .NOT(decoder_2_out2), .OR(decoder_2_out3),
    .AND(decoder_2_out4), .ADD(decoder_2_out0), .SUB(decoder_2_out1), .A(multiplexer_2_out),
    .B(multiplexer_1_out), .R(alu_1_r));  // open: C
  assign controlled_buffer_1_out = or_1_out ? not_6_out : 1'bz;  // Controlled_Buffer controlled_buffer_10
  not not_6 (not_6_out, or_1_out);
  assign controlled_buffer_2_out = undriven_6 ? alu_1_r : 8'bz;  // Controlled_Buffer controlled_buffer_11
  COUTER8 P (
    .I(undriven_8), .D(controlled_buffer_2_out), .W(undriven_7), .C(controlled_buffer_1_out), .R(RESET),
    .Q(P_q));
  // Probe on P_q
  // Probe on controlled_buffer_2_out
  assign controlled_buffer_2_out = undriven_9 ? undriven_11 : 8'bz;  // Controlled_Buffer controlled_buffer_12
  DEC4 dec4_1 (
    ._0(P_q[4]), ._1(P_q[5]), ._2(P_q[6]), ._3(P_q[7]), ._0_2(dec4_1__0_2), ._1_2(dec4_1__1_2),
    ._2_2(dec4_1__2_2), ._3_2(dec4_1__3_2), ._4(dec4_1__4), ._5(dec4_1__5), ._6(dec4_1__6), ._7(dec4_1__7),
    ._8(dec4_1__8), ._9(dec4_1__9), .A(dec4_1_a), .B(dec4_1_b), .C(dec4_1_c), .D(dec4_1_d), .E_2(dec4_1_e_2),
    .F(dec4_1_f), .E(undriven_12));
  or or_1 (or_1_out, dec4_1__7, dec4_1__1_2, dec4_1__2_2, dec4_1__3_2, dec4_1__4, dec4_1__5, dec4_1__6, dec4_1__8, dec4_1__9, dec4_1_a, dec4_1_b, dec4_1_c, dec4_1_d, dec4_1_e_2);
  RAM16 ram16_1 (
    .SELECT(dec4_1_f), .CLOCK(controlled_buffer_1_out), .WRITE(undriven_9), .RESET(RESET),
    .ADDRESS(P_q[3:0]), .IN(undriven_11), .OUT(controlled_buffer_2_out));
  ROM #(.addrWidth(4)) rom_1 (.addr(P_q[3:0]), .data(controlled_buffer_2_out), .sel(dec4_1__0_2));

  // Notes on the sheet:
  //   DATA BUS
  //   CONTROL BUS
  //   NON-EXISTING
  //   ADDRESSES
  //   contents of rom_1 (hex, n*v repeats v):
  //   4*aa
endmodule

module ALU (
  input  LSR,
  input  LSL,
  input  NOT,
  input  OR,
  input  AND,
  input  ADD,
  input  SUB,
  input  [7:0] A,
  input  [7:0] B,
  output [7:0] R,
  output C
);

  wire or_2_out;
  wire [7:0] add8_1_r, and_1_out, bit_extender_1_out, lsl_1_o, lsr_1_o, not_1_out, or_1_out, xor_1_out;

  LSR lsr_1 (.I(A), .O(lsr_1_o));
  LSL lsl_1 (.O(lsl_1_o), .I(A));
  assign R = LSR ? lsr_1_o : 8'bz;  // Controlled_Buffer controlled_buffer_1
  assign R = LSL ? lsl_1_o : 8'bz;  // Controlled_Buffer controlled_buffer_2
  assign not_1_out = ~A;  // NOT_Gate not_1, 8 bits wide
  assign R = NOT ? not_1_out : 8'bz;  // Controlled_Buffer controlled_buffer_3
  assign R = OR ? or_1_out : 8'bz;  // Controlled_Buffer controlled_buffer_4
  assign or_1_out = A | B;  // OR_Gate or_1, 8 bits wide
  assign R = AND ? and_1_out : 8'bz;  // Controlled_Buffer controlled_buffer_5
  assign and_1_out = A & B;  // AND_Gate and_1, 8 bits wide
  assign bit_extender_1_out = {{7{SUB}}, SUB};  // Bit_Extender bit_extender_1
  assign xor_1_out = B ^ bit_extender_1_out;  // XOR_Gate xor_1, 8 bits wide
  or or_2 (or_2_out, ADD, SUB);
  ADD8 add8_1 (.C(SUB), .A(A), .B(xor_1_out), .R(add8_1_r), .C_2(C));
  assign R = or_2_out ? add8_1_r : 8'bz;  // Controlled_Buffer controlled_buffer_6
endmodule

module ADD1 (
  input  Ci,
  input  A,
  input  B,
  output R,
  output Co
);

  wire and_1_out, and_2_out, xor_1_out;

  and and_1 (and_1_out, A, B);
  xor xor_1 (xor_1_out, A, B);
  xor xor_2 (R, Ci, xor_1_out);
  and and_2 (and_2_out, Ci, xor_1_out);
  or or_1 (Co, and_2_out, and_1_out);
endmodule

module ADD8 (
  input  C,
  input  [7:0] A,
  input  [7:0] B,
  output [7:0] R,
  output C_2
);

  wire add1_1_co, add1_2_co, add1_3_co, add1_4_co, add1_5_co, add1_6_co, add1_7_co;

  ADD1 add1_1 (.A(A[0]), .B(B[0]), .R(R[0]), .Ci(C), .Co(add1_1_co));
  ADD1 add1_2 (.A(A[1]), .B(B[1]), .R(R[1]), .Ci(add1_1_co), .Co(add1_2_co));
  ADD1 add1_3 (.A(A[2]), .B(B[2]), .R(R[2]), .Ci(add1_2_co), .Co(add1_3_co));
  ADD1 add1_4 (.A(A[3]), .B(B[3]), .R(R[3]), .Ci(add1_3_co), .Co(add1_4_co));
  ADD1 add1_5 (.A(A[4]), .B(B[4]), .R(R[4]), .Ci(add1_4_co), .Co(add1_5_co));
  ADD1 add1_6 (.A(A[5]), .B(B[5]), .R(R[5]), .Ci(add1_5_co), .Co(add1_6_co));
  ADD1 add1_7 (.A(A[6]), .B(B[6]), .R(R[6]), .Ci(add1_6_co), .Co(add1_7_co));
  ADD1 add1_8 (.A(A[7]), .B(B[7]), .R(R[7]), .Ci(add1_7_co), .Co(C_2));
endmodule

module LSL (
  input  [7:0] I,
  output [7:0] O
);


  assign O = {I[6:0], 1'b0};
endmodule

module LSR (
  input  [7:0] I,
  output [7:0] O
);


  assign O = {1'b0, I[7:1]};
endmodule

module SR_LATCH (
  input  S,
  input  E,
  input  R,
  output Q
);

  wire and_1_out, and_2_out, nor_1_out;

  and and_1 (and_1_out, S, E);
  and and_2 (and_2_out, E, R);
  nor nor_1 (nor_1_out, and_1_out, Q);
  nor nor_2 (Q, nor_1_out, and_2_out);
endmodule

module D_LATCH (
  input  D,
  input  E,
  input  _0,
  output Q
);

  wire and_1_out, and_2_out, nor_1_out, or_1_out;

  and and_1 (and_1_out, D, E);
  and and_2 (and_2_out, E, ~D);  // AND_Gate
  or or_1 (or_1_out, and_2_out, _0);
  nor nor_1 (nor_1_out, and_1_out, Q);
  nor nor_2 (Q, nor_1_out, or_1_out);
endmodule

module D_FLIP_FLOP (
  input  D,
  input  C,
  input  R,
  output Q
);

  wire and_1_out, and_2_out, and_3_out, and_4_out, nor_1_out, nor_2_out, nor_3_out, not_1_out, or_1_out,
       or_2_out;

  and and_1 (and_1_out, D, C);
  and and_2 (and_2_out, C, ~D);  // AND_Gate
  nor nor_1 (nor_1_out, and_1_out, nor_2_out);
  nor nor_2 (nor_2_out, nor_1_out, or_1_out);
  or or_1 (or_1_out, and_2_out, R);
  not not_1 (not_1_out, C);
  and and_3 (and_3_out, nor_2_out, not_1_out);
  and and_4 (and_4_out, not_1_out, ~nor_2_out);  // AND_Gate
  nor nor_3 (nor_3_out, and_3_out, Q);
  nor nor_4 (Q, nor_3_out, or_2_out);
  or or_2 (or_2_out, and_4_out, R);
endmodule

module REG8 (
  input  C,
  input  _0,
  input  [7:0] D,
  output [7:0] Q
);

  D_FLIP_FLOP d_flip_flop_1 (.D(D[7]), .C(C), .R(_0), .Q(Q[7]));
  D_FLIP_FLOP d_flip_flop_2 (.D(D[6]), .C(C), .R(_0), .Q(Q[6]));
  D_FLIP_FLOP d_flip_flop_3 (.D(D[5]), .C(C), .R(_0), .Q(Q[5]));
  D_FLIP_FLOP d_flip_flop_4 (.D(D[4]), .C(C), .R(_0), .Q(Q[4]));
  D_FLIP_FLOP d_flip_flop_5 (.D(D[3]), .C(C), .R(_0), .Q(Q[3]));
  D_FLIP_FLOP d_flip_flop_6 (.D(D[2]), .C(C), .R(_0), .Q(Q[2]));
  D_FLIP_FLOP d_flip_flop_7 (.D(D[0]), .C(C), .R(_0), .Q(Q[0]));
  D_FLIP_FLOP d_flip_flop_8 (.D(D[1]), .C(C), .R(_0), .Q(Q[1]));

  // Notes on the sheet:
  //   7
  //   0
endmodule

module RAM16 (
  input  SELECT,
  input  CLOCK,
  input  WRITE,
  input  RESET,
  input  [3:0] ADDRESS,
  input  [7:0] IN,
  output [7:0] OUT
);

  wire and_1_out, and_2_out, and_3_out, and_4_out, and_5_out, and_6_out, and_7_out, and_8_out, and_9_out,
       and_10_out, and_11_out, and_12_out, and_13_out, and_14_out, and_15_out, and_16_out, and_17_out,
       and_18_out, and_19_out, and_20_out, and_21_out, and_22_out, and_23_out, and_24_out, and_25_out,
       and_26_out, and_27_out, and_28_out, and_29_out, and_30_out, and_31_out, and_32_out, dec4_1__0_2,
       dec4_1__1_2, dec4_1__2_2, dec4_1__3_2, dec4_1__4, dec4_1__5, dec4_1__6, dec4_1__7, dec4_1__8,
       dec4_1__9, dec4_1_a, dec4_1_b, dec4_1_c, dec4_1_d, dec4_1_e_2, dec4_1_f;
  wire [7:0] reg8_1_q, reg8_2_q, reg8_3_q, reg8_4_q, reg8_5_q, reg8_6_q, reg8_7_q, reg8_8_q, reg8_9_q,
       reg8_10_q, reg8_11_q, reg8_12_q, reg8_13_q, reg8_14_q, reg8_15_q, reg8_16_q;

  REG8 reg8_1 (.C(and_1_out), ._0(RESET), .D(IN), .Q(reg8_1_q));
  and and_1 (and_1_out, dec4_1_f, CLOCK);
  REG8 reg8_2 (.C(and_2_out), ._0(RESET), .D(IN), .Q(reg8_2_q));
  and and_2 (and_2_out, dec4_1_e_2, CLOCK);
  REG8 reg8_3 (.C(and_3_out), ._0(RESET), .D(IN), .Q(reg8_3_q));
  and and_3 (and_3_out, dec4_1_d, CLOCK);
  REG8 reg8_4 (.C(and_4_out), ._0(RESET), .D(IN), .Q(reg8_4_q));
  and and_4 (and_4_out, dec4_1_c, CLOCK);
  REG8 reg8_5 (.C(and_5_out), ._0(RESET), .D(IN), .Q(reg8_5_q));
  and and_5 (and_5_out, dec4_1_b, CLOCK);
  REG8 reg8_6 (.C(and_6_out), ._0(RESET), .D(IN), .Q(reg8_6_q));
  and and_6 (and_6_out, dec4_1_a, CLOCK);
  REG8 reg8_7 (.C(and_7_out), ._0(RESET), .D(IN), .Q(reg8_7_q));
  and and_7 (and_7_out, dec4_1__9, CLOCK);
  REG8 reg8_8 (.C(and_8_out), ._0(RESET), .D(IN), .Q(reg8_8_q));
  and and_8 (and_8_out, dec4_1__8, CLOCK);
  DEC4 dec4_1 (
    ._0(ADDRESS[0]), ._1(ADDRESS[1]), ._2(ADDRESS[2]), ._3(ADDRESS[3]), ._0_2(dec4_1__0_2),
    ._1_2(dec4_1__1_2), ._2_2(dec4_1__2_2), ._3_2(dec4_1__3_2), ._4(dec4_1__4), ._5(dec4_1__5),
    ._6(dec4_1__6), ._7(dec4_1__7), ._8(dec4_1__8), ._9(dec4_1__9), .A(dec4_1_a), .B(dec4_1_b), .C(dec4_1_c),
    .D(dec4_1_d), .E_2(dec4_1_e_2), .F(dec4_1_f), .E(SELECT));
  assign OUT = and_9_out ? reg8_1_q : 8'bz;  // Controlled_Buffer controlled_buffer_1
  and and_9 (and_9_out, dec4_1_f, WRITE);
  assign OUT = and_10_out ? reg8_2_q : 8'bz;  // Controlled_Buffer controlled_buffer_2
  and and_10 (and_10_out, dec4_1_e_2, WRITE);
  assign OUT = and_11_out ? reg8_3_q : 8'bz;  // Controlled_Buffer controlled_buffer_3
  and and_11 (and_11_out, dec4_1_d, WRITE);
  assign OUT = and_12_out ? reg8_4_q : 8'bz;  // Controlled_Buffer controlled_buffer_4
  and and_12 (and_12_out, dec4_1_c, WRITE);
  assign OUT = and_13_out ? reg8_5_q : 8'bz;  // Controlled_Buffer controlled_buffer_5
  and and_13 (and_13_out, dec4_1_b, WRITE);
  assign OUT = and_14_out ? reg8_6_q : 8'bz;  // Controlled_Buffer controlled_buffer_6
  and and_14 (and_14_out, dec4_1_a, WRITE);
  assign OUT = and_15_out ? reg8_7_q : 8'bz;  // Controlled_Buffer controlled_buffer_7
  and and_15 (and_15_out, dec4_1__9, WRITE);
  assign OUT = and_16_out ? reg8_8_q : 8'bz;  // Controlled_Buffer controlled_buffer_8
  and and_16 (and_16_out, dec4_1__8, WRITE);
  and and_17 (and_17_out, dec4_1__0_2, WRITE);
  assign OUT = and_17_out ? reg8_9_q : 8'bz;  // Controlled_Buffer controlled_buffer_9
  and and_18 (and_18_out, dec4_1__1_2, WRITE);
  assign OUT = and_18_out ? reg8_10_q : 8'bz;  // Controlled_Buffer controlled_buffer_10
  and and_19 (and_19_out, dec4_1__2_2, WRITE);
  assign OUT = and_19_out ? reg8_11_q : 8'bz;  // Controlled_Buffer controlled_buffer_11
  and and_20 (and_20_out, dec4_1__3_2, WRITE);
  assign OUT = and_20_out ? reg8_12_q : 8'bz;  // Controlled_Buffer controlled_buffer_12
  and and_21 (and_21_out, dec4_1__4, WRITE);
  assign OUT = and_21_out ? reg8_13_q : 8'bz;  // Controlled_Buffer controlled_buffer_13
  and and_22 (and_22_out, dec4_1__5, WRITE);
  assign OUT = and_22_out ? reg8_14_q : 8'bz;  // Controlled_Buffer controlled_buffer_14
  and and_23 (and_23_out, dec4_1__6, WRITE);
  assign OUT = and_23_out ? reg8_15_q : 8'bz;  // Controlled_Buffer controlled_buffer_15
  and and_24 (and_24_out, dec4_1__7, WRITE);
  assign OUT = and_24_out ? reg8_16_q : 8'bz;  // Controlled_Buffer controlled_buffer_16
  REG8 reg8_9 (.C(and_25_out), ._0(RESET), .D(IN), .Q(reg8_9_q));
  REG8 reg8_10 (.C(and_26_out), ._0(RESET), .D(IN), .Q(reg8_10_q));
  REG8 reg8_11 (.C(and_27_out), ._0(RESET), .D(IN), .Q(reg8_11_q));
  REG8 reg8_12 (.C(and_28_out), ._0(RESET), .D(IN), .Q(reg8_12_q));
  REG8 reg8_13 (.C(and_29_out), ._0(RESET), .D(IN), .Q(reg8_13_q));
  REG8 reg8_14 (.C(and_30_out), ._0(RESET), .D(IN), .Q(reg8_14_q));
  REG8 reg8_15 (.C(and_31_out), ._0(RESET), .D(IN), .Q(reg8_15_q));
  REG8 reg8_16 (.C(and_32_out), ._0(RESET), .D(IN), .Q(reg8_16_q));
  and and_25 (and_25_out, dec4_1__0_2, CLOCK);
  and and_26 (and_26_out, dec4_1__1_2, CLOCK);
  and and_27 (and_27_out, dec4_1__2_2, CLOCK);
  and and_28 (and_28_out, dec4_1__3_2, CLOCK);
  and and_29 (and_29_out, dec4_1__4, CLOCK);
  and and_30 (and_30_out, dec4_1__5, CLOCK);
  and and_31 (and_31_out, dec4_1__6, CLOCK);
  and and_32 (and_32_out, dec4_1__7, CLOCK);

  // Notes on the sheet:
  //   OUT
  //   IN
endmodule

module DEC2 (
  input  _0,
  input  _1,
  input  E,
  output out_4,
  output out_5,
  output out_6,
  output out_7
);

  and and_1 (out_4, ~_0, ~_1, E);  // AND_Gate
  and and_2 (out_5, _0, ~_1, E);  // AND_Gate
  and and_3 (out_6, ~_0, _1, E);  // AND_Gate
  and and_4 (out_7, _0, _1, E);
endmodule

module DEC4 (
  input  _0,
  input  _1,
  input  _2,
  input  _3,
  input  E,
  output _0_2,
  output _1_2,
  output _2_2,
  output _3_2,
  output _4,
  output _5,
  output _6,
  output _7,
  output _8,
  output _9,
  output A,
  output B,
  output C,
  output D,
  output E_2,
  output F
);

  wire dec2_1_out_4, dec2_1_out_5, dec2_1_out_6, dec2_1_out_7;

  DEC2 dec2_1 (
    ._0(_2), ._1(_3), .out_4(dec2_1_out_4), .out_5(dec2_1_out_5), .out_6(dec2_1_out_6), .out_7(dec2_1_out_7),
    .E(E));
  DEC2 dec2_2 (._0(_0), ._1(_1), .out_4(_0_2), .out_5(_1_2), .out_6(_2_2), .out_7(_3_2), .E(dec2_1_out_4));
  DEC2 dec2_3 (._0(_0), ._1(_1), .out_4(_4), .out_5(_5), .out_6(_6), .out_7(_7), .E(dec2_1_out_5));
  DEC2 dec2_4 (._0(_0), ._1(_1), .out_4(_8), .out_5(_9), .out_6(A), .out_7(B), .E(dec2_1_out_6));
  DEC2 dec2_5 (._0(_0), ._1(_1), .out_4(C), .out_5(D), .out_6(E_2), .out_7(F), .E(dec2_1_out_7));
endmodule

module TOGGLE (
  input  C,
  input  R,
  input  T,
  input  W,
  input  D,
  output Q
);

  wire multiplexer_1_out, multiplexer_2_out, not_1_out;

  D_FLIP_FLOP d_flip_flop_1 (.D(multiplexer_1_out), .C(C), .R(R), .Q(Q));
  Multiplexer #(.enable("false")) multiplexer_1 (
    .in0(multiplexer_2_out), .in1(not_1_out), .out(multiplexer_1_out), .sel(T));
  not not_1 (not_1_out, Q);
  Multiplexer #(.enable("false")) multiplexer_2 (.in0(Q), .in1(D), .out(multiplexer_2_out), .sel(W));
endmodule

module COUTER8 (
  input  I,
  input  [7:0] D,
  input  W,
  input  C,
  input  R,
  output [7:0] Q
);

  wire and_1_out, and_2_out, and_3_out, and_4_out, and_5_out, and_6_out, and_7_out;

  and and_1 (and_1_out, Q[0], I);
  TOGGLE toggle_1 (.C(C), .R(R), .T(I), .D(D[0]), .Q(Q[0]), .W(W));
  TOGGLE toggle_2 (.C(C), .R(R), .T(and_1_out), .D(D[1]), .Q(Q[1]), .W(W));
  and and_2 (and_2_out, and_1_out, Q[1]);
  TOGGLE toggle_3 (.C(C), .R(R), .T(and_2_out), .D(D[2]), .Q(Q[2]), .W(W));
  and and_3 (and_3_out, and_2_out, Q[2]);
  TOGGLE toggle_4 (.C(C), .R(R), .T(and_3_out), .D(D[3]), .Q(Q[3]), .W(W));
  and and_4 (and_4_out, and_3_out, Q[3]);
  and and_5 (and_5_out, and_4_out, Q[4]);
  TOGGLE toggle_5 (.C(C), .R(R), .T(and_4_out), .D(D[4]), .Q(Q[4]), .W(W));
  TOGGLE toggle_6 (.C(C), .R(R), .T(and_5_out), .D(D[5]), .Q(Q[5]), .W(W));
  and and_6 (and_6_out, and_5_out, Q[5]);
  TOGGLE toggle_7 (.C(C), .R(R), .T(and_6_out), .D(D[6]), .Q(Q[6]), .W(W));
  and and_7 (and_7_out, and_6_out, Q[6]);
  TOGGLE toggle_8 (.C(C), .R(R), .T(and_7_out), .D(D[7]), .Q(Q[7]), .W(W));

  // Notes on the sheet:
  //   0
  //   7
endmodule
